# Fritzing sketch reloj (saved by Fritzing 0.9.3b)
breadboards: 1

parts:
  U1 = 7-SEGMENT-4DIGIT [package=7-segment-4digit-youngsun]
  Componente1 = Arduino Nano (Rev3.0)

nets:
  N1: U1.1, Componente1.D12/MISO
  N2: U1.2, Componente1.D5
  N3: U1.3, Componente1.D13/SCK
  N4: U1.4, Componente1.D4
  N5: U1.5, Componente1.D8
  N6: U1.6, Componente1.D6
  N7: U1.9, Componente1.D1/TX
  N8: U1.11, Componente1.D9
  N9: U1.13, Componente1.D10
  N10: U1.14, Componente1.D7
  N11: U1.15, Componente1.D0/RX
  N12: U1.16, Componente1.D11/MOSI
